# Fritzing sketch fabriekje (saved by Fritzing 1.0.6)

parts:
  Arduino_Nano = Arduino Nano (Rev3.0)
  4-wire_stepper = Stepper Motor - Bipolar
  part = DRV 8825 Stepper Motor Carrier, High Current [part_number="DRV 8825"]
  12V = 2.1mm Barrel Jack with Terminal Block
  C2 = Capacitor Polarized [package=cpol-radial-1000uf-25v]
  D1 = Diode [package=diode-hv]
  S1 = Pushbutton [package="[THT]"]
  BD139 = npn-Powertransistor [package="TO220 [THT]"]
  R1 = Resistor [tolerance=±5% resistance=220 package="2010 [SMD]"]
  L1 = Inductor [package="0603 [SMD]"]
  LM7805 = Voltage Regulator - 5V [package="TO220 [THT]"]

nets:
  N1: Arduino_Nano.GND, Arduino_Nano.D4, S1.Pin_1, S1.Pin_2
  N2: Arduino_Nano.D3, R1.Pin_0
  N3: Arduino_Nano.VIN, part.SLEEP, C2.+, LM7805.output_voltage
  N4: Arduino_Nano.A5, part.DIRECTION
  N5: Arduino_Nano.A4, part.STEP
  N6: 4-wire_stepper.A, part.OUT_2B
  N7: 4-wire_stepper.C, part.OUT_2A
  N8: 4-wire_stepper.B, part.OUT_1A
  N9: 4-wire_stepper.D, part.OUT_1B
  N10: part.VOLTAGE_ST/_MT, D1.C, BD139.emitter, LM7805.input_voltage
  N11: part.GROUND_LOG, L1.pin_1
  N12: 12V.POS, D1.A
  N13: 12V.NEG, C2.-, LM7805.GND
  N14: BD139.base, R1.Pin_1
  N15: BD139.collector, L1.pin_0
